# Fritzing sketch Base Machine Sequencer UI (saved by Fritzing 0.9.2b)
breadboards: 2

parts:
  U1 = mystery part, 16 pins [chip_label=CH12864F-SPI]
  R1 = Resistor [tolerance=±5% resistance=100 package=THT]
  J1 = STM32 Nucleo boards
  RE1 = Rotary Encoder [package=THT]
  RE3 = Rotary Encoder [package=THT]
  RE2 = Rotary Encoder [package=THT]
  S1 = Pushbutton [package="[THT]"]
  S2 = Pushbutton [package="[THT]"]
  S3 = Pushbutton [package="[THT]"]
  S4 = Pushbutton [package="[THT]"]
  S5 = Pushbutton [package="[THT]"]
  S6 = Pushbutton [package="[THT]"]
  S7 = Pushbutton [package="[THT]"]
  S8 = Pushbutton [package="[THT]"]
  S9 = Pushbutton [package="[THT]"]
  S10 = Pushbutton [package="[THT]"]
  R2 = Rotary Potentiometer (Small) [maximum_resistance=100kΩ package=THT]
  R3 = Rotary Potentiometer (Small) [maximum_resistance=100kΩ package=THT]
  R4 = Rotary Potentiometer (Small) [maximum_resistance=100kΩ package=THT]
  R5 = Rotary Potentiometer (Small) [maximum_resistance=100kΩ package=THT]
  R6 = Rotary Potentiometer (Small) [maximum_resistance=100kΩ package=THT]
  R7 = Rotary Potentiometer (Small) [maximum_resistance=100kΩ package=THT]

nets:
  N1: U1.pin3, J1.PB1
  N2: U1.pin4, J1.PB2
  N3: U1.pin5, J1.PB12
  N4: U1.pin6, R1.Pin_0
  N5: U1.pin7, J1.GND#1189, RE1.EncoderPinC, RE3.EncoderPinC, RE2.EncoderPinC, S1.Pin_1, S1.Pin_2, S2.Pin_1, S2.Pin_2, S3.Pin_1, S3.Pin_2, S4.Pin_1, S4.Pin_2, S5.Pin_1, S5.Pin_2, S6.Pin_1, S6.Pin_2, S7.Pin_1, S7.Pin_2, S8.Pin_1, S8.Pin_2, S9.Pin_1, S9.Pin_2, S10.Pin_1, S10.Pin_2
  N6: U1.pin8, R1.Pin_1, J1.3V3
  N7: U1.pin9, J1.PB15
  N8: U1.pin10, J1.PB13
  N9: J1.PC11, S2.Pin_3, S2.Pin_4
  N10: J1.PD2, S1.Pin_3, S1.Pin_4
  N11: J1.3v3, R2.leg2
  N12: J1.GND#339, R2.leg1
  N13: J1.PB8, RE1.EncoderPinB
  N14: J1.PB9, RE1.EncoderPinA
  N15: J1.PB4, RE2.EncoderPinB
  N16: J1.PB5, RE2.EncoderPinA
  N17: J1.PB3, RE3.EncoderPinB
  N18: J1.PA10, RE3.EncoderPinA
  N19: J1.PA0, R2.wiper
  N20: J1.PA1, R3.wiper
  N21: J1.PA4, R4.wiper
  N22: J1.PB0, R5.wiper
  N23: J1.PC1, R6.wiper
  N24: J1.PC0, R7.wiper
  N25: J1.PC10, S3.Pin_3, S3.Pin_4
  N26: J1.PC12, S4.Pin_3, S4.Pin_4
  N27: J1.PA13, S5.Pin_3, S5.Pin_4
  N28: J1.PA14, S6.Pin_3, S6.Pin_4
  N29: J1.PA15, S7.Pin_3, S7.Pin_4
  N30: J1.PB7, S8.Pin_3, S8.Pin_4
  N31: S9.Pin_3, S9.Pin_4
  N32: S10.Pin_3, S10.Pin_4

notes:
  BPM
  Pitch
  Step
  GND
  3.3V
  CH12864F-SPI
  7 SCK
  8 SI
  9 VDD
  10 VSS
  11 LEDA
  12 CS
  13 RS
  14 D/I
  3.3V
  GND
  Control Panel
