# Fritzing sketch Base Machine (saved by Fritzing 0.9.2b)
perfboards: 5

parts:
  J1 = STM32 Nucleo boards
  J2 = female pin header, 9 pins [form="♀ (female)"]  # not connected
  J3 = female pin header, 9 pins [form="♀ (female)"]  # not connected
  J4 = female pin header, 8 pins [form="♀ (female)"]
  J5 = female pin header, 8 pins [form="♀ (female)"]
  J6 = female pin header, 10 pins [form="♀ (female)"]
  J7 = female pin header, 2 pins [form="♀ (female)"]
  J8 = female pin header, 5 pins [form="♀ (female)"]
  J9 = female pin header, 3 pins [form="♀ (female)"]  # not connected
  J10 = female pin header, 3 pins [form="♀ (female)"]
  J11 = female pin header, 4 pins [form="♀ (female)"]  # not connected
  J12 = female pin header, 4 pins [form="♀ (female)"]
  J13 = female pin header, 4 pins [form="♀ (female)"]
  J14 = female pin header, 4 pins [form="♀ (female)"]
  J15 = female pin header, 2 pins [form="♀ (female)"]  # not connected
  J16 = female pin header, 2 pins [form="♀ (female)"]  # not connected
  JP1 = RCA [package=rca_lock]
  JP2 = RCA [package=rca_lock]  # not connected
  JP3 = RCA [package=rca_lock]
  JP4 = RCA [package=rca_lock]
  Power_plug1 = Power plug
  Power_plug2 = Power plug
  R1 = Rotary Potentiometer (Small) [maximum_resistance=100kΩ package=THT]  # not connected
  R2 = Rotary Potentiometer (Small) [maximum_resistance=100kΩ package=THT]  # not connected

nets:
  N1: J1.E5V, J13.pin1
  N2: J1.GND#333, J13.pin3
  N3: J1.D8, J8.pin1
  N4: J1.D9_PWM, J5.pin3
  N5: J1.D11_PWM/MOSI, J8.pin3
  N6: J1.D13/SCK, J8.pin2
  N7: J1.D7, J8.pin5
  N8: J4.pin1, J12.pin1
  N9: J4.pin2, J12.pin3
  N10: J6.pin4, J10.pin2
  N11: J6.pin6, J10.pin1
  N12: J6.pin7, J10.pin3
  N13: J7.pin2, JP3.PIN
  N14: J14.pin1, Power_plug1.GND
  N15: J14.pin2, Power_plug1.VCC
  N16: J14.pin3, Power_plug2.GND
  N17: J14.pin4, Power_plug2.VCC
  N18: JP1.PIN, JP4.SHELL
  N19: JP1.SHELL, JP4.PIN

notes:
  PSoC 4 DCO
  OTA DCA
  VCVS DCF Shield
  on Nucleo
  Arduino Header
  OUT
  IN
  5V
  Control Panel
