# Fritzing sketch st7567 & AnalogIn_Test (saved by Fritzing 0.9.2b)
breadboards: 1

parts:
  U1 = mystery part, 16 pins [chip_label=CH12864F-SPI]
  R1 = Resistor [tolerance=±5% resistance=100 package=THT]
  J1 = STM32 Nucleo boards
  R2 = Rotary Potentiometer (Small) [maximum_resistance=100kΩ package=THT]

nets:
  N1: U1.pin3, J1.PB1
  N2: U1.pin4, J1.PB2
  N3: U1.pin5, J1.PB12
  N4: U1.pin6, R1.Pin_0
  N5: U1.pin7, J1.GND, R2.leg2
  N6: U1.pin8, R1.Pin_1, J1.3V3, R2.leg1
  N7: U1.pin9, J1.PB15
  N8: U1.pin10, J1.PB13
  N9: J1.A0, R2.wiper

notes:
  CH12864F-SPI
  7 SCK
  8 SI
  9 VDD
  10 VSS
  11 LEDA
  12 CS
  13 RS
  14 D/I
